// Logisim project basicgates.circ as structural Verilog: 40 circuits, main circuit main
module main (
);

  wire [31:0] multiplier32bit_1_output1, multiplier32bit_1_overflow, multiplier_1_cout, multiplier_1_out;

  // Probe on multiplier_1_out
  Multiplier #(.width(32)) multiplier_1 (
    .a(32'hffffff44), .b(32'hffffffee), .out(multiplier_1_out), .cin(32'h1234), .cout(multiplier_1_cout));
  // Probe on multiplier_1_cout
  // Probe on multiplier32bit_1_overflow
  multiplier32bit multiplier32bit_1 (
    .inflow(32'h1234), .input1(32'hffffff44), .input2(32'hffffffee), .overflow(multiplier32bit_1_overflow),
    .output1(multiplier32bit_1_output1));
  // Probe on multiplier32bit_1_output1
endmodule

module adder1bit (
  input  inflow,
  input  input1,
  input  input2,
  output overflow,
  output output1
);

  wire and_1_out, and_2_out, xor_1_out;

  and and_1 (and_1_out, input1, input2);
  xor xor_1 (xor_1_out, input1, input2);
  and and_2 (and_2_out, inflow, xor_1_out);
  xor xor_2 (output1, inflow, xor_1_out);
  or or_1 (overflow, and_1_out, and_2_out);
endmodule

module adder2bit (
  input  inflow,
  input  [1:0] input1,
  input  [1:0] input2,
  output overflow,
  output [1:0] output1
);

  wire adder1bit_1_overflow;

  adder1bit adder1bit_1 (
    .inflow(inflow), .input1(input1[0]), .input2(input2[0]), .overflow(adder1bit_1_overflow),
    .output1(output1[0]));
  adder1bit adder1bit_2 (
    .inflow(adder1bit_1_overflow), .input1(input1[1]), .input2(input2[1]), .overflow(overflow),
    .output1(output1[1]));
endmodule

module adder4bit (
  input  inflow,
  input  [3:0] input1,
  input  [3:0] input2,
  output overflow,
  output [3:0] output1
);

  wire adder2bit_1_overflow;

  adder2bit adder2bit_1 (
    .inflow(inflow), .input1(input1[1:0]), .input2(input2[1:0]), .overflow(adder2bit_1_overflow),
    .output1(output1[1:0]));
  adder2bit adder2bit_2 (
    .inflow(adder2bit_1_overflow), .input1(input1[3:2]), .input2(input2[3:2]), .overflow(overflow),
    .output1(output1[3:2]));
endmodule

module adder8bit (
  input  inflow,
  input  [7:0] input1,
  input  [7:0] input2,
  output overflow,
  output [7:0] output1
);

  wire adder4bit_1_overflow;

  adder4bit adder4bit_1 (
    .inflow(inflow), .input1(input1[3:0]), .input2(input2[3:0]), .overflow(adder4bit_1_overflow),
    .output1(output1[3:0]));
  adder4bit adder4bit_2 (
    .inflow(adder4bit_1_overflow), .input1(input1[7:4]), .input2(input2[7:4]), .overflow(overflow),
    .output1(output1[7:4]));
endmodule

module adder16bit (
  input  inflow,
  input  [15:0] input1,
  input  [15:0] input2,
  output overflow,
  output [15:0] output1
);

  wire adder8bit_1_overflow;

  adder8bit adder8bit_1 (
    .inflow(inflow), .input1(input1[7:0]), .input2(input2[7:0]), .overflow(adder8bit_1_overflow),
    .output1(output1[7:0]));
  adder8bit adder8bit_2 (
    .inflow(adder8bit_1_overflow), .input1(input1[15:8]), .input2(input2[15:8]), .overflow(overflow),
    .output1(output1[15:8]));
endmodule

module adder32bit (
  input  inflow,
  input  [31:0] input1,
  input  [31:0] input2,
  output overflow,
  output [31:0] output1
);

  wire adder16bit_1_overflow;

  adder16bit adder16bit_1 (
    .inflow(inflow), .input1(input1[15:0]), .input2(input2[15:0]), .overflow(adder16bit_1_overflow),
    .output1(output1[15:0]));
  adder16bit adder16bit_2 (
    .inflow(adder16bit_1_overflow), .input1(input1[31:16]), .input2(input2[31:16]), .overflow(overflow),
    .output1(output1[31:16]));
endmodule

module adder64bit (
  input  inflow,
  input  [63:0] input1,
  input  [63:0] input2,
  output overflow,
  output [63:0] output1
);

  wire adder32bit_1_overflow;

  adder32bit adder32bit_1 (
    .inflow(inflow), .input1(input1[31:0]), .input2(input2[31:0]), .overflow(adder32bit_1_overflow),
    .output1(output1[31:0]));
  adder32bit adder32bit_2 (
    .inflow(adder32bit_1_overflow), .input1(input1[63:32]), .input2(input2[63:32]), .overflow(overflow),
    .output1(output1[63:32]));
endmodule

module negate1bit (
  input  input1,
  output output1
);


  assign output1 = input1;
endmodule

module negate2bit (
  input  [1:0] input1,
  output [1:0] output1
);

  wire [1:0] not_1_out;

  assign not_1_out = ~input1;  // NOT_Gate not_1, 2 bits wide
  adder2bit adder2bit_1 (.input1(2'b01), .input2(not_1_out), .output1(output1));  // open: inflow, overflow
endmodule

module negate4bit (
  input  [3:0] input1,
  output [3:0] output1
);

  wire [3:0] not_1_out;

  assign not_1_out = ~input1;  // NOT_Gate not_1, 4 bits wide
  adder4bit adder4bit_1 (.input1(4'b0001), .input2(not_1_out), .output1(output1));  // open: inflow, overflow
endmodule

module negate8bit (
  input  [7:0] input1,
  output [7:0] output1
);

  wire [7:0] not_1_out;

  assign not_1_out = ~input1;  // NOT_Gate not_1, 8 bits wide
  adder8bit adder8bit_1 (.input1(8'h1), .input2(not_1_out), .output1(output1));  // open: inflow, overflow
endmodule

module negate16bit (
  input  [15:0] input1,
  output [15:0] output1
);

  wire [15:0] not_1_out;

  assign not_1_out = ~input1;  // NOT_Gate not_1, 16 bits wide
  adder16bit adder16bit_1 (.input1(16'h1), .input2(not_1_out), .output1(output1));  // open: inflow, overflow
endmodule

module negate32bit (
  input  [31:0] input1,
  output [31:0] output1
);

  wire [31:0] not_1_out;

  assign not_1_out = ~input1;  // NOT_Gate not_1, 32 bits wide
  adder32bit adder32bit_1 (.input1(32'h1), .input2(not_1_out), .output1(output1));  // open: inflow, overflow
endmodule

module negate64bit (
  input  [63:0] input1,
  output [63:0] output1
);

  wire [63:0] not_1_out;

  assign not_1_out = ~input1;  // NOT_Gate not_1, 64 bits wide
  adder64bit adder64bit_1 (.input1(64'h1), .input2(not_1_out), .output1(output1));  // open: inflow, overflow
endmodule

module subtractor1bit (
  input  inborrow,
  input  input1,
  input  input2,
  output borrow,
  output output1
);

  wire and_1_out, and_2_out, not_1_out, not_2_out, xor_1_out;

  not not_1 (not_1_out, input1);
  xor xor_1 (xor_1_out, input1, input2);
  and and_1 (and_1_out, not_1_out, input2);
  and and_2 (and_2_out, inborrow, not_2_out);
  not not_2 (not_2_out, xor_1_out);
  xor xor_2 (output1, inborrow, xor_1_out);
  or or_1 (borrow, and_1_out, and_2_out);
endmodule

module subtractor2bit (
  input  inborrow,
  input  [1:0] input1,
  input  [1:0] input2,
  output borrow,
  output [1:0] output1
);

  wire subtractor1bit_1_borrow;

  subtractor1bit subtractor1bit_1 (
    .inborrow(inborrow), .input1(input1[0]), .input2(input2[0]), .borrow(subtractor1bit_1_borrow),
    .output1(output1[0]));
  subtractor1bit subtractor1bit_2 (
    .inborrow(subtractor1bit_1_borrow), .input1(input1[1]), .input2(input2[1]), .borrow(borrow),
    .output1(output1[1]));
endmodule

module subtractor4bit (
  input  inborrow,
  input  [3:0] input1,
  input  [3:0] input2,
  output borrow,
  output [3:0] output1
);

  wire subtractor2bit_1_borrow;

  subtractor2bit subtractor2bit_1 (
    .inborrow(inborrow), .input1(input1[1:0]), .input2(input2[1:0]), .borrow(subtractor2bit_1_borrow),
    .output1(output1[1:0]));
  subtractor2bit subtractor2bit_2 (
    .inborrow(subtractor2bit_1_borrow), .input1(input1[3:2]), .input2(input2[3:2]), .borrow(borrow),
    .output1(output1[3:2]));
endmodule

module subtractor8bit (
  input  inborrow,
  input  [7:0] input1,
  input  [7:0] input2,
  output borrow,
  output [7:0] output1
);

  wire subtractor4bit_1_borrow;

  subtractor4bit subtractor4bit_1 (
    .inborrow(inborrow), .input1(input1[3:0]), .input2(input2[3:0]), .borrow(subtractor4bit_1_borrow),
    .output1(output1[3:0]));
  subtractor4bit subtractor4bit_2 (
    .inborrow(subtractor4bit_1_borrow), .input1(input1[7:4]), .input2(input2[7:4]), .borrow(borrow),
    .output1(output1[7:4]));
endmodule

module subtractor16bit (
  input  inborrow,
  input  [15:0] input1,
  input  [15:0] input2,
  output borrow,
  output [15:0] output1
);

  wire subtractor8bit_1_borrow;

  subtractor8bit subtractor8bit_1 (
    .inborrow(inborrow), .input1(input1[7:0]), .input2(input2[7:0]), .borrow(subtractor8bit_1_borrow),
    .output1(output1[7:0]));
  subtractor8bit subtractor8bit_2 (
    .inborrow(subtractor8bit_1_borrow), .input1(input1[15:8]), .input2(input2[15:8]), .borrow(borrow),
    .output1(output1[15:8]));
endmodule

module subtractor32bit (
  input  inborrow,
  input  [31:0] input1,
  input  [31:0] input2,
  output borrow,
  output [31:0] output1
);

  wire subtractor16bit_1_borrow;

  subtractor16bit subtractor16bit_1 (
    .inborrow(inborrow), .input1(input1[15:0]), .input2(input2[15:0]), .borrow(subtractor16bit_1_borrow),
    .output1(output1[15:0]));
  subtractor16bit subtractor16bit_2 (
    .inborrow(subtractor16bit_1_borrow), .input1(input1[31:16]), .input2(input2[31:16]), .borrow(borrow),
    .output1(output1[31:16]));
endmodule

module subtractor64bit (
  input  inborrow,
  input  [63:0] input1,
  input  [63:0] input2,
  output borrow,
  output [63:0] output1
);

  wire subtractor32bit_1_borrow;

  subtractor32bit subtractor32bit_1 (
    .inborrow(inborrow), .input1(input1[31:0]), .input2(input2[31:0]), .borrow(subtractor32bit_1_borrow),
    .output1(output1[31:0]));
  subtractor32bit subtractor32bit_2 (
    .inborrow(subtractor32bit_1_borrow), .input1(input1[63:32]), .input2(input2[63:32]), .borrow(borrow),
    .output1(output1[63:32]));
endmodule

module multiplier64bit (
  input  [63:0] inflow,
  input  [63:0] input1,
  input  [63:0] input2,
  output [63:0] overflow,
  output [63:0] output1
);

  wire [63:0] adder128bit_1_output1a, adder128bit_1_output1b, adder128bit_2_output1a, adder128bit_2_output1b,
       adder128bit_3_output1a, adder128bit_3_output1b, adder128bit_4_output1a, adder128bit_4_output1b,
       adder128bit_5_output1a, adder128bit_5_output1b, adder128bit_6_output1a, adder128bit_6_output1b,
       adder128bit_7_output1a, adder128bit_7_output1b, adder128bit_8_output1a, adder128bit_8_output1b,
       adder128bit_9_output1a, adder128bit_9_output1b, adder128bit_10_output1a, adder128bit_10_output1b,
       adder128bit_11_output1a, adder128bit_11_output1b, adder128bit_12_output1a, adder128bit_12_output1b,
       adder128bit_13_output1a, adder128bit_13_output1b, adder128bit_14_output1a, adder128bit_14_output1b,
       adder128bit_15_output1a, adder128bit_15_output1b, adder128bit_16_output1a, adder128bit_16_output1b,
       adder128bit_17_output1a, adder128bit_17_output1b, adder128bit_18_output1a, adder128bit_18_output1b,
       adder128bit_19_output1a, adder128bit_19_output1b, adder128bit_20_output1a, adder128bit_20_output1b,
       adder128bit_21_output1a, adder128bit_21_output1b, adder128bit_22_output1a, adder128bit_22_output1b,
       adder128bit_23_output1a, adder128bit_23_output1b, adder128bit_24_output1a, adder128bit_24_output1b,
       adder128bit_25_output1a, adder128bit_25_output1b, adder128bit_26_output1a, adder128bit_26_output1b,
       adder128bit_27_output1a, adder128bit_27_output1b, adder128bit_28_output1a, adder128bit_28_output1b,
       adder128bit_29_output1a, adder128bit_29_output1b, adder128bit_30_output1a, adder128bit_30_output1b,
       adder128bit_31_output1a, adder128bit_31_output1b, adder128bit_33_output1a, adder128bit_33_output1b,
       adder128bit_34_output1a, adder128bit_34_output1b, adder128bit_35_output1a, adder128bit_35_output1b,
       adder128bit_36_output1a, adder128bit_36_output1b, adder128bit_37_output1a, adder128bit_37_output1b,
       adder128bit_38_output1a, adder128bit_38_output1b, adder128bit_39_output1a, adder128bit_39_output1b,
       adder128bit_40_output1a, adder128bit_40_output1b, adder128bit_41_output1a, adder128bit_41_output1b,
       adder128bit_42_output1a, adder128bit_42_output1b, adder128bit_43_output1a, adder128bit_43_output1b,
       adder128bit_44_output1a, adder128bit_44_output1b, adder128bit_45_output1a, adder128bit_45_output1b,
       adder128bit_46_output1a, adder128bit_46_output1b, adder128bit_47_output1a, adder128bit_47_output1b,
       adder128bit_48_output1a, adder128bit_48_output1b, adder128bit_49_output1a, adder128bit_49_output1b,
       adder128bit_50_output1a, adder128bit_50_output1b, adder128bit_51_output1a, adder128bit_51_output1b,
       adder128bit_52_output1a, adder128bit_52_output1b, adder128bit_53_output1a, adder128bit_53_output1b,
       adder128bit_54_output1a, adder128bit_54_output1b, adder128bit_55_output1a, adder128bit_55_output1b,
       adder128bit_56_output1a, adder128bit_56_output1b, adder128bit_57_output1a, adder128bit_57_output1b,
       adder128bit_58_output1a, adder128bit_58_output1b, adder128bit_59_output1a, adder128bit_59_output1b,
       adder128bit_60_output1a, adder128bit_60_output1b, adder128bit_61_output1a, adder128bit_61_output1b,
       adder128bit_62_output1a, adder128bit_62_output1b, adder128bit_63_output1a, adder128bit_63_output1b,
       adder128bit_64_output1a, adder128bit_64_output1b, controlled_buffer_1_out, controlled_buffer_8_out,
       controlled_buffer_16_out, controlled_buffer_24_out, controlled_buffer_32_out,
       controlled_buffer_40_out, controlled_buffer_48_out, controlled_buffer_56_out, pull_resistor_1_node,
       pull_resistor_2_node, pull_resistor_3_node, pull_resistor_5_node, pull_resistor_6_node,
       pull_resistor_7_node, pull_resistor_8_node, pull_resistor_9_node, pull_resistor_10_node,
       pull_resistor_11_node, pull_resistor_13_node, pull_resistor_14_node, pull_resistor_15_node,
       pull_resistor_16_node, pull_resistor_17_node, pull_resistor_18_node, pull_resistor_19_node,
       pull_resistor_21_node, pull_resistor_22_node, pull_resistor_23_node, pull_resistor_24_node,
       pull_resistor_25_node, pull_resistor_26_node, pull_resistor_27_node, pull_resistor_29_node,
       pull_resistor_30_node, pull_resistor_31_node, pull_resistor_32_node, pull_resistor_33_node,
       pull_resistor_34_node, pull_resistor_35_node, pull_resistor_37_node, pull_resistor_38_node,
       pull_resistor_39_node, pull_resistor_40_node, pull_resistor_41_node, pull_resistor_42_node,
       pull_resistor_43_node, pull_resistor_45_node, pull_resistor_46_node, pull_resistor_47_node,
       pull_resistor_48_node, pull_resistor_49_node, pull_resistor_50_node, pull_resistor_51_node,
       pull_resistor_53_node, pull_resistor_54_node, pull_resistor_55_node, pull_resistor_56_node,
       pull_resistor_57_node, pull_resistor_58_node, pull_resistor_59_node, pull_resistor_61_node,
       pull_resistor_62_node, pull_resistor_63_node, pull_resistor_64_node, pull_resistor_65_node,
       pull_resistor_66_node, pull_resistor_67_node, pull_resistor_68_node, pull_resistor_69_node,
       pull_resistor_70_node, pull_resistor_71_node, pull_resistor_72_node, pull_resistor_73_node,
       pull_resistor_74_node, pull_resistor_75_node, pull_resistor_76_node, pull_resistor_77_node,
       pull_resistor_78_node, pull_resistor_79_node, pull_resistor_80_node, pull_resistor_81_node,
       pull_resistor_82_node, pull_resistor_83_node, pull_resistor_84_node, pull_resistor_85_node,
       pull_resistor_86_node, pull_resistor_87_node, pull_resistor_88_node, pull_resistor_89_node,
       pull_resistor_90_node, pull_resistor_91_node, pull_resistor_92_node, pull_resistor_93_node,
       pull_resistor_94_node, pull_resistor_95_node, pull_resistor_96_node, pull_resistor_97_node,
       pull_resistor_98_node, pull_resistor_99_node, pull_resistor_100_node, pull_resistor_101_node,
       pull_resistor_102_node, pull_resistor_103_node, pull_resistor_104_node, pull_resistor_105_node,
       pull_resistor_106_node, pull_resistor_107_node, pull_resistor_108_node, pull_resistor_109_node,
       pull_resistor_110_node, pull_resistor_111_node, pull_resistor_112_node, pull_resistor_113_node,
       pull_resistor_114_node, pull_resistor_115_node, pull_resistor_116_node, pull_resistor_117_node,
       pull_resistor_118_node, pull_resistor_119_node, pull_resistor_120_node, pull_resistor_121_node,
       pull_resistor_122_node, pull_resistor_123_node, pull_resistor_124_node, pull_resistor_125_node,
       pull_resistor_126_node, pull_resistor_127_node;

  adder128bit adder128bit_1 (
    .input1a(pull_resistor_64_node), .input1b(pull_resistor_1_node), .input2a(pull_resistor_65_node),
    .input2b(controlled_buffer_1_out), .output1a(adder128bit_1_output1a), .output1b(adder128bit_1_output1b));  // open: inflow, overflow
  Pull_Resistor pull_resistor_1 (.node(pull_resistor_1_node));
  assign controlled_buffer_1_out = input1[62] ? {2'b00, input2[63:2]} : 64'bz;  // Controlled_Buffer controlled_buffer_1
  assign pull_resistor_1_node = input1[63] ? {1'b0, input2[63:1]} : 64'bz;  // Controlled_Buffer controlled_buffer_2
  adder128bit adder128bit_2 (
    .input1a(pull_resistor_66_node), .input1b(pull_resistor_3_node), .input2a(pull_resistor_67_node),
    .input2b(pull_resistor_2_node), .output1a(adder128bit_2_output1a), .output1b(adder128bit_2_output1b));  // open: inflow, overflow
  Pull_Resistor pull_resistor_2 (.node(pull_resistor_2_node));
  Pull_Resistor pull_resistor_3 (.node(pull_resistor_3_node));
  Pull_Resistor pull_resistor_4 (.node(controlled_buffer_1_out));
  assign pull_resistor_2_node = input1[60] ? {4'b0000, input2[63:4]} : 64'bz;  // Controlled_Buffer controlled_buffer_3
  assign pull_resistor_3_node = input1[61] ? {3'b000, input2[63:3]} : 64'bz;  // Controlled_Buffer controlled_buffer_4
  adder128bit adder128bit_3 (
    .input1a(pull_resistor_68_node), .input1b(pull_resistor_7_node), .input2a(pull_resistor_69_node),
    .input2b(pull_resistor_6_node), .output1a(adder128bit_3_output1a), .output1b(adder128bit_3_output1b));  // open: inflow, overflow
  Pull_Resistor pull_resistor_5 (.node(pull_resistor_5_node));
  Pull_Resistor pull_resistor_6 (.node(pull_resistor_6_node));
  Pull_Resistor pull_resistor_7 (.node(pull_resistor_7_node));
  assign pull_resistor_5_node = input1[57] ? {{7{1'b0}}, input2[63:7]} : 64'bz;  // Controlled_Buffer controlled_buffer_5
  assign pull_resistor_6_node = input1[58] ? {{6{1'b0}}, input2[63:6]} : 64'bz;  // Controlled_Buffer controlled_buffer_6
  assign pull_resistor_7_node = input1[59] ? {{5{1'b0}}, input2[63:5]} : 64'bz;  // Controlled_Buffer controlled_buffer_7
  Pull_Resistor pull_resistor_8 (.node(pull_resistor_8_node));
  Pull_Resistor pull_resistor_9 (.node(pull_resistor_9_node));
  assign controlled_buffer_8_out = input1[54] ? {{10{1'b0}}, input2[63:10]} : 64'bz;  // Controlled_Buffer controlled_buffer_8
  assign pull_resistor_8_node = input1[55] ? {{9{1'b0}}, input2[63:9]} : 64'bz;  // Controlled_Buffer controlled_buffer_9
  assign pull_resistor_9_node = input1[56] ? {{8{1'b0}}, input2[63:8]} : 64'bz;  // Controlled_Buffer controlled_buffer_10
  adder128bit adder128bit_4 (
    .input1a(pull_resistor_70_node), .input1b(pull_resistor_5_node), .input2a(pull_resistor_71_node),
    .input2b(pull_resistor_9_node), .output1a(adder128bit_4_output1a), .output1b(adder128bit_4_output1b));  // open: inflow, overflow
  Pull_Resistor pull_resistor_10 (.node(pull_resistor_10_node));
  Pull_Resistor pull_resistor_11 (.node(pull_resistor_11_node));
  Pull_Resistor pull_resistor_12 (.node(controlled_buffer_8_out));
  assign pull_resistor_10_node = input1[52] ? {{12{1'b0}}, input2[63:12]} : 64'bz;  // Controlled_Buffer controlled_buffer_11
  assign pull_resistor_11_node = input1[53] ? {{11{1'b0}}, input2[63:11]} : 64'bz;  // Controlled_Buffer controlled_buffer_12
  adder128bit adder128bit_5 (
    .input1a(pull_resistor_72_node), .input1b(pull_resistor_8_node), .input2a(pull_resistor_73_node),
    .input2b(controlled_buffer_8_out), .output1a(adder128bit_5_output1a), .output1b(adder128bit_5_output1b));  // open: inflow, overflow
  Pull_Resistor pull_resistor_13 (.node(pull_resistor_13_node));
  Pull_Resistor pull_resistor_14 (.node(pull_resistor_14_node));
  Pull_Resistor pull_resistor_15 (.node(pull_resistor_15_node));
  assign pull_resistor_13_node = input1[49] ? {{15{1'b0}}, input2[63:15]} : 64'bz;  // Controlled_Buffer controlled_buffer_13
  assign pull_resistor_14_node = input1[50] ? {{14{1'b0}}, input2[63:14]} : 64'bz;  // Controlled_Buffer controlled_buffer_14
  assign pull_resistor_15_node = input1[51] ? {{13{1'b0}}, input2[63:13]} : 64'bz;  // Controlled_Buffer controlled_buffer_15
  Pull_Resistor pull_resistor_16 (.node(pull_resistor_16_node));
  Pull_Resistor pull_resistor_17 (.node(pull_resistor_17_node));
  assign controlled_buffer_16_out = input1[46] ? {{18{1'b0}}, input2[63:18]} : 64'bz;  // Controlled_Buffer controlled_buffer_16
  assign pull_resistor_16_node = input1[47] ? {{17{1'b0}}, input2[63:17]} : 64'bz;  // Controlled_Buffer controlled_buffer_17
  assign pull_resistor_17_node = input1[48] ? {{16{1'b0}}, input2[63:16]} : 64'bz;  // Controlled_Buffer controlled_buffer_18
  adder128bit adder128bit_6 (
    .input1a(pull_resistor_74_node), .input1b(pull_resistor_11_node), .input2a(pull_resistor_75_node),
    .input2b(pull_resistor_10_node), .output1a(adder128bit_6_output1a), .output1b(adder128bit_6_output1b));  // open: inflow, overflow
  Pull_Resistor pull_resistor_18 (.node(pull_resistor_18_node));
  Pull_Resistor pull_resistor_19 (.node(pull_resistor_19_node));
  Pull_Resistor pull_resistor_20 (.node(controlled_buffer_16_out));
  assign pull_resistor_18_node = input1[44] ? {{20{1'b0}}, input2[63:20]} : 64'bz;  // Controlled_Buffer controlled_buffer_19
  assign pull_resistor_19_node = input1[45] ? {{19{1'b0}}, input2[63:19]} : 64'bz;  // Controlled_Buffer controlled_buffer_20
  Pull_Resistor pull_resistor_21 (.node(pull_resistor_21_node));
  Pull_Resistor pull_resistor_22 (.node(pull_resistor_22_node));
  Pull_Resistor pull_resistor_23 (.node(pull_resistor_23_node));
  assign pull_resistor_21_node = input1[41] ? {{23{1'b0}}, input2[63:23]} : 64'bz;  // Controlled_Buffer controlled_buffer_21
  assign pull_resistor_22_node = input1[42] ? {{22{1'b0}}, input2[63:22]} : 64'bz;  // Controlled_Buffer controlled_buffer_22
  assign pull_resistor_23_node = input1[43] ? {{21{1'b0}}, input2[63:21]} : 64'bz;  // Controlled_Buffer controlled_buffer_23
  adder128bit adder128bit_7 (
    .input1a(pull_resistor_76_node), .input1b(pull_resistor_15_node), .input2a(pull_resistor_77_node),
    .input2b(pull_resistor_14_node), .output1a(adder128bit_7_output1a), .output1b(adder128bit_7_output1b));  // open: inflow, overflow
  Pull_Resistor pull_resistor_24 (.node(pull_resistor_24_node));
  Pull_Resistor pull_resistor_25 (.node(pull_resistor_25_node));
  assign controlled_buffer_24_out = input1[38] ? {{26{1'b0}}, input2[63:26]} : 64'bz;  // Controlled_Buffer controlled_buffer_24
  assign pull_resistor_24_node = input1[39] ? {{25{1'b0}}, input2[63:25]} : 64'bz;  // Controlled_Buffer controlled_buffer_25
  assign pull_resistor_25_node = input1[40] ? {{24{1'b0}}, input2[63:24]} : 64'bz;  // Controlled_Buffer controlled_buffer_26
  adder128bit adder128bit_8 (
    .input1a(pull_resistor_78_node), .input1b(pull_resistor_13_node), .input2a(pull_resistor_79_node),
    .input2b(pull_resistor_17_node), .output1a(adder128bit_8_output1a), .output1b(adder128bit_8_output1b));  // open: inflow, overflow
  Pull_Resistor pull_resistor_26 (.node(pull_resistor_26_node));
  Pull_Resistor pull_resistor_27 (.node(pull_resistor_27_node));
  Pull_Resistor pull_resistor_28 (.node(controlled_buffer_24_out));
  assign pull_resistor_26_node = input1[36] ? {{28{1'b0}}, input2[63:28]} : 64'bz;  // Controlled_Buffer controlled_buffer_27
  assign pull_resistor_27_node = input1[37] ? {{27{1'b0}}, input2[63:27]} : 64'bz;  // Controlled_Buffer controlled_buffer_28
  Pull_Resistor pull_resistor_29 (.node(pull_resistor_29_node));
  Pull_Resistor pull_resistor_30 (.node(pull_resistor_30_node));
  Pull_Resistor pull_resistor_31 (.node(pull_resistor_31_node));
  assign pull_resistor_29_node = input1[33] ? {{31{1'b0}}, input2[63:31]} : 64'bz;  // Controlled_Buffer controlled_buffer_29
  assign pull_resistor_30_node = input1[34] ? {{30{1'b0}}, input2[63:30]} : 64'bz;  // Controlled_Buffer controlled_buffer_30
  assign pull_resistor_31_node = input1[35] ? {{29{1'b0}}, input2[63:29]} : 64'bz;  // Controlled_Buffer controlled_buffer_31
  adder128bit adder128bit_9 (
    .input1a(adder128bit_1_output1a), .input1b(adder128bit_1_output1b), .input2a(adder128bit_2_output1a),
    .input2b(adder128bit_2_output1b), .output1a(adder128bit_9_output1a), .output1b(adder128bit_9_output1b));  // open: inflow, overflow
  adder128bit adder128bit_10 (
    .input1a(pull_resistor_80_node), .input1b(pull_resistor_16_node), .input2a(pull_resistor_81_node),
    .input2b(controlled_buffer_16_out), .output1a(adder128bit_10_output1a), .output1b(adder128bit_10_output1b));  // open: inflow, overflow
  Pull_Resistor pull_resistor_32 (.node(pull_resistor_32_node));
  Pull_Resistor pull_resistor_33 (.node(pull_resistor_33_node));
  assign controlled_buffer_32_out = input1[30] ? {{34{1'b0}}, input2[63:34]} : 64'bz;  // Controlled_Buffer controlled_buffer_32
  assign pull_resistor_32_node = input1[31] ? {{33{1'b0}}, input2[63:33]} : 64'bz;  // Controlled_Buffer controlled_buffer_33
  assign pull_resistor_33_node = input1[32] ? {{32{1'b0}}, input2[63:32]} : 64'bz;  // Controlled_Buffer controlled_buffer_34
  Pull_Resistor pull_resistor_34 (.node(pull_resistor_34_node));
  Pull_Resistor pull_resistor_35 (.node(pull_resistor_35_node));
  Pull_Resistor pull_resistor_36 (.node(controlled_buffer_32_out));
  assign pull_resistor_34_node = input1[28] ? {{36{1'b0}}, input2[63:36]} : 64'bz;  // Controlled_Buffer controlled_buffer_35
  assign pull_resistor_35_node = input1[29] ? {{35{1'b0}}, input2[63:35]} : 64'bz;  // Controlled_Buffer controlled_buffer_36
  adder128bit adder128bit_11 (
    .input1a(adder128bit_3_output1a), .input1b(adder128bit_3_output1b), .input2a(adder128bit_4_output1a),
    .input2b(adder128bit_4_output1b), .output1a(adder128bit_11_output1a), .output1b(adder128bit_11_output1b));  // open: inflow, overflow
  adder128bit adder128bit_12 (
    .input1a(pull_resistor_82_node), .input1b(pull_resistor_19_node), .input2a(pull_resistor_83_node),
    .input2b(pull_resistor_18_node), .output1a(adder128bit_12_output1a), .output1b(adder128bit_12_output1b));  // open: inflow, overflow
  Pull_Resistor pull_resistor_37 (.node(pull_resistor_37_node));
  Pull_Resistor pull_resistor_38 (.node(pull_resistor_38_node));
  Pull_Resistor pull_resistor_39 (.node(pull_resistor_39_node));
  assign pull_resistor_37_node = input1[25] ? {{39{1'b0}}, input2[63:39]} : 64'bz;  // Controlled_Buffer controlled_buffer_37
  assign pull_resistor_38_node = input1[26] ? {{38{1'b0}}, input2[63:38]} : 64'bz;  // Controlled_Buffer controlled_buffer_38
  assign pull_resistor_39_node = input1[27] ? {{37{1'b0}}, input2[63:37]} : 64'bz;  // Controlled_Buffer controlled_buffer_39
  adder128bit adder128bit_13 (
    .input1a(adder128bit_5_output1a), .input1b(adder128bit_5_output1b), .input2a(adder128bit_6_output1a),
    .input2b(adder128bit_6_output1b), .output1a(adder128bit_13_output1a), .output1b(adder128bit_13_output1b));  // open: inflow, overflow
  adder128bit adder128bit_14 (
    .input1a(pull_resistor_84_node), .input1b(pull_resistor_23_node), .input2a(pull_resistor_85_node),
    .input2b(pull_resistor_22_node), .output1a(adder128bit_14_output1a), .output1b(adder128bit_14_output1b));  // open: inflow, overflow
  Pull_Resistor pull_resistor_40 (.node(pull_resistor_40_node));
  Pull_Resistor pull_resistor_41 (.node(pull_resistor_41_node));
  assign controlled_buffer_40_out = input1[22] ? {{42{1'b0}}, input2[63:42]} : 64'bz;  // Controlled_Buffer controlled_buffer_40
  assign pull_resistor_40_node = input1[23] ? {{41{1'b0}}, input2[63:41]} : 64'bz;  // Controlled_Buffer controlled_buffer_41
  assign pull_resistor_41_node = input1[24] ? {{40{1'b0}}, input2[63:40]} : 64'bz;  // Controlled_Buffer controlled_buffer_42
  Pull_Resistor pull_resistor_42 (.node(pull_resistor_42_node));
  Pull_Resistor pull_resistor_43 (.node(pull_resistor_43_node));
  Pull_Resistor pull_resistor_44 (.node(controlled_buffer_40_out));
  assign pull_resistor_42_node = input1[20] ? {{44{1'b0}}, input2[63:44]} : 64'bz;  // Controlled_Buffer controlled_buffer_43
  assign pull_resistor_43_node = input1[21] ? {{43{1'b0}}, input2[63:43]} : 64'bz;  // Controlled_Buffer controlled_buffer_44
  adder128bit adder128bit_15 (
    .input1a(adder128bit_7_output1a), .input1b(adder128bit_7_output1b), .input2a(adder128bit_8_output1a),
    .input2b(adder128bit_8_output1b), .output1a(adder128bit_15_output1a), .output1b(adder128bit_15_output1b));  // open: inflow, overflow
  adder128bit adder128bit_16 (
    .input1a(pull_resistor_86_node), .input1b(pull_resistor_21_node), .input2a(pull_resistor_87_node),
    .input2b(pull_resistor_25_node), .output1a(adder128bit_16_output1a), .output1b(adder128bit_16_output1b));  // open: inflow, overflow
  Pull_Resistor pull_resistor_45 (.node(pull_resistor_45_node));
  Pull_Resistor pull_resistor_46 (.node(pull_resistor_46_node));
  Pull_Resistor pull_resistor_47 (.node(pull_resistor_47_node));
  assign pull_resistor_45_node = input1[17] ? {{47{1'b0}}, input2[63:47]} : 64'bz;  // Controlled_Buffer controlled_buffer_45
  assign pull_resistor_46_node = input1[18] ? {{46{1'b0}}, input2[63:46]} : 64'bz;  // Controlled_Buffer controlled_buffer_46
  assign pull_resistor_47_node = input1[19] ? {{45{1'b0}}, input2[63:45]} : 64'bz;  // Controlled_Buffer controlled_buffer_47
  adder128bit adder128bit_17 (
    .input1a(adder128bit_9_output1a), .input1b(adder128bit_9_output1b), .input2a(adder128bit_11_output1a),
    .input2b(adder128bit_11_output1b), .output1a(adder128bit_17_output1a), .output1b(adder128bit_17_output1b));  // open: inflow, overflow
  adder128bit adder128bit_18 (
    .input1a(adder128bit_10_output1a), .input1b(adder128bit_10_output1b), .input2a(adder128bit_12_output1a),
    .input2b(adder128bit_12_output1b), .output1a(adder128bit_18_output1a), .output1b(adder128bit_18_output1b));  // open: inflow, overflow
  adder128bit adder128bit_19 (
    .input1a(pull_resistor_88_node), .input1b(pull_resistor_24_node), .input2a(pull_resistor_89_node),
    .input2b(controlled_buffer_24_out), .output1a(adder128bit_19_output1a), .output1b(adder128bit_19_output1b));  // open: inflow, overflow
  Pull_Resistor pull_resistor_48 (.node(pull_resistor_48_node));
  Pull_Resistor pull_resistor_49 (.node(pull_resistor_49_node));
  assign controlled_buffer_48_out = input1[14] ? {{50{1'b0}}, input2[63:50]} : 64'bz;  // Controlled_Buffer controlled_buffer_48
  assign pull_resistor_48_node = input1[15] ? {{49{1'b0}}, input2[63:49]} : 64'bz;  // Controlled_Buffer controlled_buffer_49
  assign pull_resistor_49_node = input1[16] ? {{48{1'b0}}, input2[63:48]} : 64'bz;  // Controlled_Buffer controlled_buffer_50
  Pull_Resistor pull_resistor_50 (.node(pull_resistor_50_node));
  Pull_Resistor pull_resistor_51 (.node(pull_resistor_51_node));
  Pull_Resistor pull_resistor_52 (.node(controlled_buffer_48_out));
  assign pull_resistor_50_node = input1[12] ? {{52{1'b0}}, input2[63:52]} : 64'bz;  // Controlled_Buffer controlled_buffer_51
  assign pull_resistor_51_node = input1[13] ? {{51{1'b0}}, input2[63:51]} : 64'bz;  // Controlled_Buffer controlled_buffer_52
  adder128bit adder128bit_20 (
    .input1a(adder128bit_13_output1a), .input1b(adder128bit_13_output1b), .input2a(adder128bit_15_output1a),
    .input2b(adder128bit_15_output1b), .output1a(adder128bit_20_output1a), .output1b(adder128bit_20_output1b));  // open: inflow, overflow
  adder128bit adder128bit_21 (
    .input1a(adder128bit_14_output1a), .input1b(adder128bit_14_output1b), .input2a(adder128bit_16_output1a),
    .input2b(adder128bit_16_output1b), .output1a(adder128bit_21_output1a), .output1b(adder128bit_21_output1b));  // open: inflow, overflow
  adder128bit adder128bit_22 (
    .input1a(pull_resistor_90_node), .input1b(pull_resistor_27_node), .input2a(pull_resistor_91_node),
    .input2b(pull_resistor_26_node), .output1a(adder128bit_22_output1a), .output1b(adder128bit_22_output1b));  // open: inflow, overflow
  Pull_Resistor pull_resistor_53 (.node(pull_resistor_53_node));
  Pull_Resistor pull_resistor_54 (.node(pull_resistor_54_node));
  Pull_Resistor pull_resistor_55 (.node(pull_resistor_55_node));
  assign pull_resistor_53_node = input1[9] ? {{55{1'b0}}, input2[63:55]} : 64'bz;  // Controlled_Buffer controlled_buffer_53
  assign pull_resistor_54_node = input1[10] ? {{54{1'b0}}, input2[63:54]} : 64'bz;  // Controlled_Buffer controlled_buffer_54
  assign pull_resistor_55_node = input1[11] ? {{53{1'b0}}, input2[63:53]} : 64'bz;  // Controlled_Buffer controlled_buffer_55
  Pull_Resistor pull_resistor_56 (.node(pull_resistor_56_node));
  Pull_Resistor pull_resistor_57 (.node(pull_resistor_57_node));
  assign controlled_buffer_56_out = input1[6] ? {{58{1'b0}}, input2[63:58]} : 64'bz;  // Controlled_Buffer controlled_buffer_56
  assign pull_resistor_56_node = input1[7] ? {{57{1'b0}}, input2[63:57]} : 64'bz;  // Controlled_Buffer controlled_buffer_57
  assign pull_resistor_57_node = input1[8] ? {{56{1'b0}}, input2[63:56]} : 64'bz;  // Controlled_Buffer controlled_buffer_58
  adder128bit adder128bit_23 (
    .input1a(adder128bit_17_output1a), .input1b(adder128bit_17_output1b), .input2a(adder128bit_20_output1a),
    .input2b(adder128bit_20_output1b), .output1a(adder128bit_23_output1a), .output1b(adder128bit_23_output1b));  // open: inflow, overflow
  adder128bit adder128bit_24 (
    .input1a(adder128bit_18_output1a), .input1b(adder128bit_18_output1b), .input2a(adder128bit_21_output1a),
    .input2b(adder128bit_21_output1b), .output1a(adder128bit_24_output1a), .output1b(adder128bit_24_output1b));  // open: inflow, overflow
  adder128bit adder128bit_25 (
    .input1a(adder128bit_19_output1a), .input1b(adder128bit_19_output1b), .input2a(adder128bit_22_output1a),
    .input2b(adder128bit_22_output1b), .output1a(adder128bit_25_output1a), .output1b(adder128bit_25_output1b));  // open: inflow, overflow
  adder128bit adder128bit_26 (
    .input1a(pull_resistor_92_node), .input1b(pull_resistor_31_node), .input2a(pull_resistor_93_node),
    .input2b(pull_resistor_30_node), .output1a(adder128bit_26_output1a), .output1b(adder128bit_26_output1b));  // open: inflow, overflow
  Pull_Resistor pull_resistor_58 (.node(pull_resistor_58_node));
  Pull_Resistor pull_resistor_59 (.node(pull_resistor_59_node));
  Pull_Resistor pull_resistor_60 (.node(controlled_buffer_56_out));
  assign pull_resistor_58_node = input1[4] ? {{60{1'b0}}, input2[63:60]} : 64'bz;  // Controlled_Buffer controlled_buffer_59
  assign pull_resistor_59_node = input1[5] ? {{59{1'b0}}, input2[63:59]} : 64'bz;  // Controlled_Buffer controlled_buffer_60
  adder128bit adder128bit_27 (
    .input1a(adder128bit_23_output1a), .input1b(adder128bit_23_output1b), .input2a(adder128bit_28_output1a),
    .input2b(adder128bit_28_output1b), .output1a(adder128bit_27_output1a), .output1b(adder128bit_27_output1b));  // open: inflow, overflow
  adder128bit adder128bit_28 (
    .input1a(adder128bit_24_output1a), .input1b(adder128bit_24_output1b), .input2a(adder128bit_29_output1a),
    .input2b(adder128bit_29_output1b), .output1a(adder128bit_28_output1a), .output1b(adder128bit_28_output1b));  // open: inflow, overflow
  adder128bit adder128bit_29 (
    .input1a(adder128bit_25_output1a), .input1b(adder128bit_25_output1b), .input2a(adder128bit_30_output1a),
    .input2b(adder128bit_30_output1b), .output1a(adder128bit_29_output1a), .output1b(adder128bit_29_output1b));  // open: inflow, overflow
  adder128bit adder128bit_30 (
    .input1a(adder128bit_26_output1a), .input1b(adder128bit_26_output1b), .input2a(adder128bit_31_output1a),
    .input2b(adder128bit_31_output1b), .output1a(adder128bit_30_output1a), .output1b(adder128bit_30_output1b));  // open: inflow, overflow
  adder128bit adder128bit_31 (
    .input1a(pull_resistor_94_node), .input1b(pull_resistor_29_node), .input2a(pull_resistor_95_node),
    .input2b(pull_resistor_33_node), .output1a(adder128bit_31_output1a), .output1b(adder128bit_31_output1b));  // open: inflow, overflow
  Pull_Resistor pull_resistor_61 (.node(pull_resistor_61_node));
  Pull_Resistor pull_resistor_62 (.node(pull_resistor_62_node));
  Pull_Resistor pull_resistor_63 (.node(pull_resistor_63_node));
  assign pull_resistor_61_node = input1[1] ? {{63{1'b0}}, input2[63]} : 64'bz;  // Controlled_Buffer controlled_buffer_61
  assign pull_resistor_62_node = input1[2] ? {{62{1'b0}}, input2[63:62]} : 64'bz;  // Controlled_Buffer controlled_buffer_62
  assign pull_resistor_63_node = input1[3] ? {{61{1'b0}}, input2[63:61]} : 64'bz;  // Controlled_Buffer controlled_buffer_63
  adder128bit adder128bit_32 (
    .input1a(adder128bit_27_output1a), .input1b(adder128bit_27_output1b), .input2a(adder128bit_33_output1a),
    .input2b(adder128bit_33_output1b), .output1a(output1), .output1b(overflow));  // open: inflow, overflow
  adder128bit adder128bit_33 (
    .input1a(adder128bit_34_output1a), .input1b(adder128bit_34_output1b), .input2a(adder128bit_38_output1a),
    .input2b(adder128bit_38_output1b), .output1a(adder128bit_33_output1a), .output1b(adder128bit_33_output1b));  // open: inflow, overflow
  adder128bit adder128bit_34 (
    .input1a(adder128bit_35_output1a), .input1b(adder128bit_35_output1b), .input2a(adder128bit_39_output1a),
    .input2b(adder128bit_39_output1b), .output1a(adder128bit_34_output1a), .output1b(adder128bit_34_output1b));  // open: inflow, overflow
  adder128bit adder128bit_35 (
    .input1a(adder128bit_36_output1a), .input1b(adder128bit_36_output1b), .input2a(adder128bit_40_output1a),
    .input2b(adder128bit_40_output1b), .output1a(adder128bit_35_output1a), .output1b(adder128bit_35_output1b));  // open: inflow, overflow
  adder128bit adder128bit_36 (
    .input1a(adder128bit_37_output1a), .input1b(adder128bit_37_output1b), .input2a(adder128bit_41_output1a),
    .input2b(adder128bit_41_output1b), .output1a(adder128bit_36_output1a), .output1b(adder128bit_36_output1b));  // open: inflow, overflow
  adder128bit adder128bit_37 (
    .input1a(pull_resistor_96_node), .input1b(pull_resistor_32_node), .input2a(pull_resistor_97_node),
    .input2b(controlled_buffer_32_out), .output1a(adder128bit_37_output1a), .output1b(adder128bit_37_output1b));  // open: inflow, overflow
  Pull_Resistor pull_resistor_64 (.node(pull_resistor_64_node));
  Pull_Resistor pull_resistor_65 (.node(pull_resistor_65_node));
  Pull_Resistor pull_resistor_66 (.node(pull_resistor_66_node));
  assign pull_resistor_64_node = input1[0] ? input2 : 64'bz;  // Controlled_Buffer controlled_buffer_64
  assign pull_resistor_65_node = input1[1] ? {input2[62:0], 1'b0} : 64'bz;  // Controlled_Buffer controlled_buffer_65
  Pull_Resistor pull_resistor_67 (.node(pull_resistor_67_node));
  Pull_Resistor pull_resistor_68 (.node(pull_resistor_68_node));
  assign pull_resistor_66_node = input1[2] ? {input2[61:0], 2'b00} : 64'bz;  // Controlled_Buffer controlled_buffer_66
  assign pull_resistor_67_node = input1[3] ? {input2[60:0], 3'b000} : 64'bz;  // Controlled_Buffer controlled_buffer_67
  assign pull_resistor_68_node = input1[4] ? {input2[59:0], 4'b0000} : 64'bz;  // Controlled_Buffer controlled_buffer_68
  adder128bit adder128bit_38 (
    .input1a(adder128bit_42_output1a), .input1b(adder128bit_42_output1b), .input2a(adder128bit_45_output1a),
    .input2b(adder128bit_45_output1b), .output1a(adder128bit_38_output1a), .output1b(adder128bit_38_output1b));  // open: inflow, overflow
  adder128bit adder128bit_39 (
    .input1a(adder128bit_43_output1a), .input1b(adder128bit_43_output1b), .input2a(adder128bit_46_output1a),
    .input2b(adder128bit_46_output1b), .output1a(adder128bit_39_output1a), .output1b(adder128bit_39_output1b));  // open: inflow, overflow
  adder128bit adder128bit_40 (
    .input1a(adder128bit_44_output1a), .input1b(adder128bit_44_output1b), .input2a(adder128bit_47_output1a),
    .input2b(adder128bit_47_output1b), .output1a(adder128bit_40_output1a), .output1b(adder128bit_40_output1b));  // open: inflow, overflow
  adder128bit adder128bit_41 (
    .input1a(pull_resistor_98_node), .input1b(pull_resistor_35_node), .input2a(pull_resistor_99_node),
    .input2b(pull_resistor_34_node), .output1a(adder128bit_41_output1a), .output1b(adder128bit_41_output1b));  // open: inflow, overflow
  Pull_Resistor pull_resistor_69 (.node(pull_resistor_69_node));
  Pull_Resistor pull_resistor_70 (.node(pull_resistor_70_node));
  Pull_Resistor pull_resistor_71 (.node(pull_resistor_71_node));
  assign pull_resistor_69_node = input1[5] ? {input2[58:0], {5{1'b0}}} : 64'bz;  // Controlled_Buffer controlled_buffer_69
  assign pull_resistor_70_node = input1[6] ? {input2[57:0], {6{1'b0}}} : 64'bz;  // Controlled_Buffer controlled_buffer_70
  assign pull_resistor_71_node = input1[7] ? {input2[56:0], {7{1'b0}}} : 64'bz;  // Controlled_Buffer controlled_buffer_71
  adder128bit adder128bit_42 (
    .input1a(adder128bit_48_output1a), .input1b(adder128bit_48_output1b), .input2a(adder128bit_50_output1a),
    .input2b(adder128bit_50_output1b), .output1a(adder128bit_42_output1a), .output1b(adder128bit_42_output1b));  // open: inflow, overflow
  adder128bit adder128bit_43 (
    .input1a(adder128bit_49_output1a), .input1b(adder128bit_49_output1b), .input2a(adder128bit_51_output1a),
    .input2b(adder128bit_51_output1b), .output1a(adder128bit_43_output1a), .output1b(adder128bit_43_output1b));  // open: inflow, overflow
  adder128bit adder128bit_44 (
    .input1a(pull_resistor_100_node), .input1b(pull_resistor_39_node), .input2a(pull_resistor_101_node),
    .input2b(pull_resistor_38_node), .output1a(adder128bit_44_output1a), .output1b(adder128bit_44_output1b));  // open: inflow, overflow
  Pull_Resistor pull_resistor_72 (.node(pull_resistor_72_node));
  Pull_Resistor pull_resistor_73 (.node(pull_resistor_73_node));
  Pull_Resistor pull_resistor_74 (.node(pull_resistor_74_node));
  assign pull_resistor_72_node = input1[8] ? {input2[55:0], {8{1'b0}}} : 64'bz;  // Controlled_Buffer controlled_buffer_72
  assign pull_resistor_73_node = input1[9] ? {input2[54:0], {9{1'b0}}} : 64'bz;  // Controlled_Buffer controlled_buffer_73
  Pull_Resistor pull_resistor_75 (.node(pull_resistor_75_node));
  Pull_Resistor pull_resistor_76 (.node(pull_resistor_76_node));
  assign pull_resistor_74_node = input1[10] ? {input2[53:0], {10{1'b0}}} : 64'bz;  // Controlled_Buffer controlled_buffer_74
  assign pull_resistor_75_node = input1[11] ? {input2[52:0], {11{1'b0}}} : 64'bz;  // Controlled_Buffer controlled_buffer_75
  assign pull_resistor_76_node = input1[12] ? {input2[51:0], {12{1'b0}}} : 64'bz;  // Controlled_Buffer controlled_buffer_76
  adder128bit adder128bit_45 (
    .input1a(adder128bit_52_output1a), .input1b(adder128bit_52_output1b), .input2a(adder128bit_54_output1a),
    .input2b(adder128bit_54_output1b), .output1a(adder128bit_45_output1a), .output1b(adder128bit_45_output1b));  // open: inflow, overflow
  adder128bit adder128bit_46 (
    .input1a(adder128bit_53_output1a), .input1b(adder128bit_53_output1b), .input2a(adder128bit_55_output1a),
    .input2b(adder128bit_55_output1b), .output1a(adder128bit_46_output1a), .output1b(adder128bit_46_output1b));  // open: inflow, overflow
  adder128bit adder128bit_47 (
    .input1a(pull_resistor_102_node), .input1b(pull_resistor_37_node), .input2a(pull_resistor_103_node),
    .input2b(pull_resistor_41_node), .output1a(adder128bit_47_output1a), .output1b(adder128bit_47_output1b));  // open: inflow, overflow
  Pull_Resistor pull_resistor_77 (.node(pull_resistor_77_node));
  Pull_Resistor pull_resistor_78 (.node(pull_resistor_78_node));
  Pull_Resistor pull_resistor_79 (.node(pull_resistor_79_node));
  assign pull_resistor_77_node = input1[13] ? {input2[50:0], {13{1'b0}}} : 64'bz;  // Controlled_Buffer controlled_buffer_77
  assign pull_resistor_78_node = input1[14] ? {input2[49:0], {14{1'b0}}} : 64'bz;  // Controlled_Buffer controlled_buffer_78
  assign pull_resistor_79_node = input1[15] ? {input2[48:0], {15{1'b0}}} : 64'bz;  // Controlled_Buffer controlled_buffer_79
  adder128bit adder128bit_48 (
    .input1a(adder128bit_56_output1a), .input1b(adder128bit_56_output1b), .input2a(adder128bit_57_output1a),
    .input2b(adder128bit_57_output1b), .output1a(adder128bit_48_output1a), .output1b(adder128bit_48_output1b));  // open: inflow, overflow
  adder128bit adder128bit_49 (
    .input1a(pull_resistor_104_node), .input1b(pull_resistor_40_node), .input2a(pull_resistor_105_node),
    .input2b(controlled_buffer_40_out), .output1a(adder128bit_49_output1a), .output1b(adder128bit_49_output1b));  // open: inflow, overflow
  Pull_Resistor pull_resistor_80 (.node(pull_resistor_80_node));
  Pull_Resistor pull_resistor_81 (.node(pull_resistor_81_node));
  Pull_Resistor pull_resistor_82 (.node(pull_resistor_82_node));
  assign pull_resistor_80_node = input1[16] ? {input2[47:0], {16{1'b0}}} : 64'bz;  // Controlled_Buffer controlled_buffer_80
  assign pull_resistor_81_node = input1[17] ? {input2[46:0], {17{1'b0}}} : 64'bz;  // Controlled_Buffer controlled_buffer_81
  Pull_Resistor pull_resistor_83 (.node(pull_resistor_83_node));
  Pull_Resistor pull_resistor_84 (.node(pull_resistor_84_node));
  assign pull_resistor_82_node = input1[18] ? {input2[45:0], {18{1'b0}}} : 64'bz;  // Controlled_Buffer controlled_buffer_82
  assign pull_resistor_83_node = input1[19] ? {input2[44:0], {19{1'b0}}} : 64'bz;  // Controlled_Buffer controlled_buffer_83
  assign pull_resistor_84_node = input1[20] ? {input2[43:0], {20{1'b0}}} : 64'bz;  // Controlled_Buffer controlled_buffer_84
  adder128bit adder128bit_50 (
    .input1a(adder128bit_58_output1a), .input1b(adder128bit_58_output1b), .input2a(adder128bit_59_output1a),
    .input2b(adder128bit_59_output1b), .output1a(adder128bit_50_output1a), .output1b(adder128bit_50_output1b));  // open: inflow, overflow
  adder128bit adder128bit_51 (
    .input1a(pull_resistor_106_node), .input1b(pull_resistor_43_node), .input2a(pull_resistor_107_node),
    .input2b(pull_resistor_42_node), .output1a(adder128bit_51_output1a), .output1b(adder128bit_51_output1b));  // open: inflow, overflow
  Pull_Resistor pull_resistor_85 (.node(pull_resistor_85_node));
  Pull_Resistor pull_resistor_86 (.node(pull_resistor_86_node));
  Pull_Resistor pull_resistor_87 (.node(pull_resistor_87_node));
  assign pull_resistor_85_node = input1[21] ? {input2[42:0], {21{1'b0}}} : 64'bz;  // Controlled_Buffer controlled_buffer_85
  assign pull_resistor_86_node = input1[22] ? {input2[41:0], {22{1'b0}}} : 64'bz;  // Controlled_Buffer controlled_buffer_86
  assign pull_resistor_87_node = input1[23] ? {input2[40:0], {23{1'b0}}} : 64'bz;  // Controlled_Buffer controlled_buffer_87
  Pull_Resistor pull_resistor_88 (.node(pull_resistor_88_node));
  Pull_Resistor pull_resistor_89 (.node(pull_resistor_89_node));
  Pull_Resistor pull_resistor_90 (.node(pull_resistor_90_node));
  assign pull_resistor_88_node = input1[24] ? {input2[39:0], {24{1'b0}}} : 64'bz;  // Controlled_Buffer controlled_buffer_88
  assign pull_resistor_89_node = input1[25] ? {input2[38:0], {25{1'b0}}} : 64'bz;  // Controlled_Buffer controlled_buffer_89
  adder128bit adder128bit_52 (
    .input1a(adder128bit_60_output1a), .input1b(adder128bit_60_output1b), .input2a(adder128bit_61_output1a),
    .input2b(adder128bit_61_output1b), .output1a(adder128bit_52_output1a), .output1b(adder128bit_52_output1b));  // open: inflow, overflow
  adder128bit adder128bit_53 (
    .input1a(pull_resistor_108_node), .input1b(pull_resistor_47_node), .input2a(pull_resistor_109_node),
    .input2b(pull_resistor_46_node), .output1a(adder128bit_53_output1a), .output1b(adder128bit_53_output1b));  // open: inflow, overflow
  Pull_Resistor pull_resistor_91 (.node(pull_resistor_91_node));
  Pull_Resistor pull_resistor_92 (.node(pull_resistor_92_node));
  assign pull_resistor_90_node = input1[26] ? {input2[37:0], {26{1'b0}}} : 64'bz;  // Controlled_Buffer controlled_buffer_90
  assign pull_resistor_91_node = input1[27] ? {input2[36:0], {27{1'b0}}} : 64'bz;  // Controlled_Buffer controlled_buffer_91
  assign pull_resistor_92_node = input1[28] ? {input2[35:0], {28{1'b0}}} : 64'bz;  // Controlled_Buffer controlled_buffer_92
  adder128bit adder128bit_54 (
    .input1a(adder128bit_62_output1a), .input1b(adder128bit_62_output1b), .input2a(adder128bit_63_output1a),
    .input2b(adder128bit_63_output1b), .output1a(adder128bit_54_output1a), .output1b(adder128bit_54_output1b));  // open: inflow, overflow
  adder128bit adder128bit_55 (
    .input1a(pull_resistor_110_node), .input1b(pull_resistor_45_node), .input2a(pull_resistor_111_node),
    .input2b(pull_resistor_49_node), .output1a(adder128bit_55_output1a), .output1b(adder128bit_55_output1b));  // open: inflow, overflow
  Pull_Resistor pull_resistor_93 (.node(pull_resistor_93_node));
  Pull_Resistor pull_resistor_94 (.node(pull_resistor_94_node));
  Pull_Resistor pull_resistor_95 (.node(pull_resistor_95_node));
  assign pull_resistor_93_node = input1[29] ? {input2[34:0], {29{1'b0}}} : 64'bz;  // Controlled_Buffer controlled_buffer_93
  assign pull_resistor_94_node = input1[30] ? {input2[33:0], {30{1'b0}}} : 64'bz;  // Controlled_Buffer controlled_buffer_94
  assign pull_resistor_95_node = input1[31] ? {input2[32:0], {31{1'b0}}} : 64'bz;  // Controlled_Buffer controlled_buffer_95
  Pull_Resistor pull_resistor_96 (.node(pull_resistor_96_node));
  Pull_Resistor pull_resistor_97 (.node(pull_resistor_97_node));
  Pull_Resistor pull_resistor_98 (.node(pull_resistor_98_node));
  assign pull_resistor_96_node = input1[32] ? {input2[31:0], {32{1'b0}}} : 64'bz;  // Controlled_Buffer controlled_buffer_96
  assign pull_resistor_97_node = input1[33] ? {input2[30:0], {33{1'b0}}} : 64'bz;  // Controlled_Buffer controlled_buffer_97
  adder128bit adder128bit_56 (
    .input1a(pull_resistor_112_node), .input1b(pull_resistor_48_node), .input2a(pull_resistor_113_node),
    .input2b(controlled_buffer_48_out), .output1a(adder128bit_56_output1a), .output1b(adder128bit_56_output1b));  // open: inflow, overflow
  Pull_Resistor pull_resistor_99 (.node(pull_resistor_99_node));
  Pull_Resistor pull_resistor_100 (.node(pull_resistor_100_node));
  assign pull_resistor_98_node = input1[34] ? {input2[29:0], {34{1'b0}}} : 64'bz;  // Controlled_Buffer controlled_buffer_98
  assign pull_resistor_99_node = input1[35] ? {input2[28:0], {35{1'b0}}} : 64'bz;  // Controlled_Buffer controlled_buffer_99
  assign pull_resistor_100_node = input1[36] ? {input2[27:0], {36{1'b0}}} : 64'bz;  // Controlled_Buffer controlled_buffer_100
  Pull_Resistor pull_resistor_101 (.node(pull_resistor_101_node));
  Pull_Resistor pull_resistor_102 (.node(pull_resistor_102_node));
  Pull_Resistor pull_resistor_103 (.node(pull_resistor_103_node));
  assign pull_resistor_101_node = input1[37] ? {input2[26:0], {37{1'b0}}} : 64'bz;  // Controlled_Buffer controlled_buffer_101
  assign pull_resistor_102_node = input1[38] ? {input2[25:0], {38{1'b0}}} : 64'bz;  // Controlled_Buffer controlled_buffer_102
  assign pull_resistor_103_node = input1[39] ? {input2[24:0], {39{1'b0}}} : 64'bz;  // Controlled_Buffer controlled_buffer_103
  adder128bit adder128bit_57 (
    .input1a(pull_resistor_114_node), .input1b(pull_resistor_51_node), .input2a(pull_resistor_115_node),
    .input2b(pull_resistor_50_node), .output1a(adder128bit_57_output1a), .output1b(adder128bit_57_output1b));  // open: inflow, overflow
  Pull_Resistor pull_resistor_104 (.node(pull_resistor_104_node));
  Pull_Resistor pull_resistor_105 (.node(pull_resistor_105_node));
  Pull_Resistor pull_resistor_106 (.node(pull_resistor_106_node));
  assign pull_resistor_104_node = input1[40] ? {input2[23:0], {40{1'b0}}} : 64'bz;  // Controlled_Buffer controlled_buffer_104
  assign pull_resistor_105_node = input1[41] ? {input2[22:0], {41{1'b0}}} : 64'bz;  // Controlled_Buffer controlled_buffer_105
  adder128bit adder128bit_58 (
    .input1a(pull_resistor_116_node), .input1b(pull_resistor_55_node), .input2a(pull_resistor_117_node),
    .input2b(pull_resistor_54_node), .output1a(adder128bit_58_output1a), .output1b(adder128bit_58_output1b));  // open: inflow, overflow
  Pull_Resistor pull_resistor_107 (.node(pull_resistor_107_node));
  Pull_Resistor pull_resistor_108 (.node(pull_resistor_108_node));
  assign pull_resistor_106_node = input1[42] ? {input2[21:0], {42{1'b0}}} : 64'bz;  // Controlled_Buffer controlled_buffer_106
  assign pull_resistor_107_node = input1[43] ? {input2[20:0], {43{1'b0}}} : 64'bz;  // Controlled_Buffer controlled_buffer_107
  assign pull_resistor_108_node = input1[44] ? {input2[19:0], {44{1'b0}}} : 64'bz;  // Controlled_Buffer controlled_buffer_108
  Pull_Resistor pull_resistor_109 (.node(pull_resistor_109_node));
  Pull_Resistor pull_resistor_110 (.node(pull_resistor_110_node));
  Pull_Resistor pull_resistor_111 (.node(pull_resistor_111_node));
  assign pull_resistor_109_node = input1[45] ? {input2[18:0], {45{1'b0}}} : 64'bz;  // Controlled_Buffer controlled_buffer_109
  assign pull_resistor_110_node = input1[46] ? {input2[17:0], {46{1'b0}}} : 64'bz;  // Controlled_Buffer controlled_buffer_110
  assign pull_resistor_111_node = input1[47] ? {input2[16:0], {47{1'b0}}} : 64'bz;  // Controlled_Buffer controlled_buffer_111
  adder128bit adder128bit_59 (
    .input1a(pull_resistor_118_node), .input1b(pull_resistor_53_node), .input2a(pull_resistor_119_node),
    .input2b(pull_resistor_57_node), .output1a(adder128bit_59_output1a), .output1b(adder128bit_59_output1b));  // open: inflow, overflow
  Pull_Resistor pull_resistor_112 (.node(pull_resistor_112_node));
  Pull_Resistor pull_resistor_113 (.node(pull_resistor_113_node));
  Pull_Resistor pull_resistor_114 (.node(pull_resistor_114_node));
  assign pull_resistor_112_node = input1[48] ? {input2[15:0], {48{1'b0}}} : 64'bz;  // Controlled_Buffer controlled_buffer_112
  assign pull_resistor_113_node = input1[49] ? {input2[14:0], {49{1'b0}}} : 64'bz;  // Controlled_Buffer controlled_buffer_113
  adder128bit adder128bit_60 (
    .input1a(pull_resistor_120_node), .input1b(pull_resistor_56_node), .input2a(pull_resistor_121_node),
    .input2b(controlled_buffer_56_out), .output1a(adder128bit_60_output1a), .output1b(adder128bit_60_output1b));  // open: inflow, overflow
  Pull_Resistor pull_resistor_115 (.node(pull_resistor_115_node));
  Pull_Resistor pull_resistor_116 (.node(pull_resistor_116_node));
  assign pull_resistor_114_node = input1[50] ? {input2[13:0], {50{1'b0}}} : 64'bz;  // Controlled_Buffer controlled_buffer_114
  assign pull_resistor_115_node = input1[51] ? {input2[12:0], {51{1'b0}}} : 64'bz;  // Controlled_Buffer controlled_buffer_115
  assign pull_resistor_116_node = input1[52] ? {input2[11:0], {52{1'b0}}} : 64'bz;  // Controlled_Buffer controlled_buffer_116
  Pull_Resistor pull_resistor_117 (.node(pull_resistor_117_node));
  Pull_Resistor pull_resistor_118 (.node(pull_resistor_118_node));
  Pull_Resistor pull_resistor_119 (.node(pull_resistor_119_node));
  assign pull_resistor_117_node = input1[53] ? {input2[10:0], {53{1'b0}}} : 64'bz;  // Controlled_Buffer controlled_buffer_117
  assign pull_resistor_118_node = input1[54] ? {input2[9:0], {54{1'b0}}} : 64'bz;  // Controlled_Buffer controlled_buffer_118
  assign pull_resistor_119_node = input1[55] ? {input2[8:0], {55{1'b0}}} : 64'bz;  // Controlled_Buffer controlled_buffer_119
  adder128bit adder128bit_61 (
    .input1a(pull_resistor_122_node), .input1b(pull_resistor_59_node), .input2a(pull_resistor_123_node),
    .input2b(pull_resistor_58_node), .output1a(adder128bit_61_output1a), .output1b(adder128bit_61_output1b));  // open: inflow, overflow
  Pull_Resistor pull_resistor_120 (.node(pull_resistor_120_node));
  Pull_Resistor pull_resistor_121 (.node(pull_resistor_121_node));
  Pull_Resistor pull_resistor_122 (.node(pull_resistor_122_node));
  assign pull_resistor_120_node = input1[56] ? {input2[7:0], {56{1'b0}}} : 64'bz;  // Controlled_Buffer controlled_buffer_120
  assign pull_resistor_121_node = input1[57] ? {input2[6:0], {57{1'b0}}} : 64'bz;  // Controlled_Buffer controlled_buffer_121
  Pull_Resistor pull_resistor_123 (.node(pull_resistor_123_node));
  Pull_Resistor pull_resistor_124 (.node(pull_resistor_124_node));
  assign pull_resistor_122_node = input1[58] ? {input2[5:0], {58{1'b0}}} : 64'bz;  // Controlled_Buffer controlled_buffer_122
  assign pull_resistor_123_node = input1[59] ? {input2[4:0], {59{1'b0}}} : 64'bz;  // Controlled_Buffer controlled_buffer_123
  assign pull_resistor_124_node = input1[60] ? {input2[3:0], {60{1'b0}}} : 64'bz;  // Controlled_Buffer controlled_buffer_124
  adder128bit adder128bit_62 (
    .input1a(pull_resistor_124_node), .input1b(pull_resistor_63_node), .input2a(pull_resistor_125_node),
    .input2b(pull_resistor_62_node), .output1a(adder128bit_62_output1a), .output1b(adder128bit_62_output1b));  // open: inflow, overflow
  Pull_Resistor pull_resistor_125 (.node(pull_resistor_125_node));
  Pull_Resistor pull_resistor_126 (.node(pull_resistor_126_node));
  Pull_Resistor pull_resistor_127 (.node(pull_resistor_127_node));
  assign pull_resistor_125_node = input1[61] ? {input2[2:0], {61{1'b0}}} : 64'bz;  // Controlled_Buffer controlled_buffer_125
  assign pull_resistor_126_node = input1[62] ? {input2[1:0], {62{1'b0}}} : 64'bz;  // Controlled_Buffer controlled_buffer_126
  assign pull_resistor_127_node = input1[63] ? {input2[0], {63{1'b0}}} : 64'bz;  // Controlled_Buffer controlled_buffer_127
  adder128bit adder128bit_63 (
    .input1a(adder128bit_64_output1a), .input1b(adder128bit_64_output1b), .input2a(inflow),
    .output1a(adder128bit_63_output1a), .output1b(adder128bit_63_output1b));  // open: inflow, input2b, overflow
  adder128bit adder128bit_64 (
    .input1a(pull_resistor_126_node), .input1b(pull_resistor_61_node), .input2a(pull_resistor_127_node),
    .output1a(adder128bit_64_output1a), .output1b(adder128bit_64_output1b));  // open: inflow, input2b, overflow
endmodule

module adder128bit (
  input  inflow,
  input  [63:0] input1a,
  input  [63:0] input1b,
  input  [63:0] input2a,
  input  [63:0] input2b,
  output overflow,
  output [63:0] output1a,
  output [63:0] output1b
);

  wire adder64bit_1_overflow;

  adder64bit adder64bit_1 (
    .inflow(inflow), .input1(input1a), .input2(input2a), .overflow(adder64bit_1_overflow), .output1(output1a));
  adder64bit adder64bit_2 (
    .inflow(adder64bit_1_overflow), .input1(input1b), .input2(input2b), .overflow(overflow),
    .output1(output1b));
endmodule

module negate128bit (
  input  [63:0] input1a,
  input  [63:0] input1b,
  output [63:0] output1a,
  output [63:0] output1b
);

  wire [63:0] not_1_out, not_2_out;

  assign not_1_out = ~input1a;  // NOT_Gate not_1, 64 bits wide
  assign not_2_out = ~input1b;  // NOT_Gate not_2, 64 bits wide
  adder128bit adder128bit_1 (
    .input1a(64'h1), .input2a(not_1_out), .input2b(not_2_out), .output1a(output1a), .output1b(output1b));  // open: inflow, input1b, overflow
endmodule

module subtractor128bit (
  input  inborrow,
  input  [63:0] input1a,
  input  [63:0] input1b,
  input  [63:0] input2a,
  input  [63:0] input2b,
  output borrow,
  output [63:0] output1a,
  output [63:0] output1b
);

  wire subtractor64bit_1_borrow;

  subtractor64bit subtractor64bit_1 (
    .inborrow(inborrow), .input1(input1a), .input2(input2a), .borrow(subtractor64bit_1_borrow),
    .output1(output1a));
  subtractor64bit subtractor64bit_2 (
    .inborrow(subtractor64bit_1_borrow), .input1(input1b), .input2(input2b), .borrow(borrow),
    .output1(output1b));
endmodule

module cbuffer1bit (
  input  buffer1,
  input  input1,
  output output1
);

  and and_1 (output1, buffer1, input1);
endmodule

module cbuffer2bit (
  input  buffer1,
  input  [1:0] input1,
  output [1:0] output1
);

  assign output1 = {2{buffer1}} & input1;  // AND_Gate and_1, 2 bits wide
endmodule

module cbuffer4bit (
  input  buffer1,
  input  [3:0] input1,
  output [3:0] output1
);

  assign output1 = {4{buffer1}} & input1;  // AND_Gate and_1, 4 bits wide
endmodule

module cbuffer8bit (
  input  buffer1,
  input  [7:0] input1,
  output [7:0] output1
);

  assign output1 = {8{buffer1}} & input1;  // AND_Gate and_1, 8 bits wide
endmodule

module cbuffer16bit (
  input  buffer1,
  input  [15:0] input1,
  output [15:0] output1
);

  assign output1 = {16{buffer1}} & input1;  // AND_Gate and_1, 16 bits wide
endmodule

module cbuffer32bit (
  input  buffer1,
  input  [31:0] input1,
  output [31:0] output1
);

  assign output1 = {32{buffer1}} & input1;  // AND_Gate and_1, 32 bits wide
endmodule

module cbuffer64bit (
  input  buffer1,
  input  [63:0] input1,
  output [63:0] output1
);

  assign output1 = {64{buffer1}} & input1;  // AND_Gate and_1, 64 bits wide
endmodule

module cbuffer128bit (
  input  buffer1,
  input  [63:0] input1a,
  input  [63:0] input1b,
  output [63:0] output1a,
  output [63:0] output1b
);

  assign output1a = {64{buffer1}} & input1a;  // AND_Gate and_1, 64 bits wide
  assign output1b = {64{buffer1}} & input1b;  // AND_Gate and_2, 64 bits wide
endmodule

module multiplier1bit (
  input  inflow,
  input  input1,
  input  input2,
  output overflow,
  output output1
);

  wire and_1_out;

  and and_1 (and_1_out, input1, input2);
  xor xor_1 (output1, inflow, and_1_out);
  and and_2 (overflow, inflow, and_1_out);
endmodule

module multiplier2bit (
  input  [1:0] inflow,
  input  [1:0] input1,
  input  [1:0] input2,
  output [1:0] overflow,
  output [1:0] output1
);

  wire [3:0] adder4bit_2_output1, cbuffer4bit_1_output1, cbuffer4bit_2_output1;

  adder4bit adder4bit_1 (
    .input1({2'b00, inflow}), .input2(adder4bit_2_output1), .output1({overflow, output1}));  // open: inflow, overflow
  cbuffer4bit cbuffer4bit_1 (.buffer1(input1[0]), .input1({2'b00, input2}), .output1(cbuffer4bit_1_output1));
  adder4bit adder4bit_2 (
    .input1(cbuffer4bit_1_output1), .input2(cbuffer4bit_2_output1), .output1(adder4bit_2_output1));  // open: inflow, overflow
  cbuffer4bit cbuffer4bit_2 (.buffer1(input1[1]), .input1({1'b0, input2, 1'b0}), .output1(cbuffer4bit_2_output1));
endmodule

module multiplier4bit (
  input  [3:0] inflow,
  input  [3:0] input1,
  input  [3:0] input2,
  output [3:0] overflow,
  output [3:0] output1
);

  wire [1:0] multiplier2bit_1_output1, multiplier2bit_1_overflow;
  wire [5:2] multiplier2bit_2_output1, multiplier2bit_3_output1;
  wire [7:0] adder8bit_1_output1, adder8bit_3_output1, adder8bit_4_output1;
  wire [7:4] multiplier2bit_4_output1;

  adder8bit adder8bit_1 (
    .input1({4'b0000, multiplier2bit_1_overflow, multiplier2bit_1_output1}),
    .input2({2'b00, multiplier2bit_2_output1, 2'b00}), .output1(adder8bit_1_output1));  // open: inflow, overflow
  multiplier2bit multiplier2bit_1 (
    .input1(input1[1:0]), .input2(input2[1:0]), .overflow(multiplier2bit_1_overflow),
    .output1(multiplier2bit_1_output1));  // open: inflow
  adder8bit adder8bit_2 (
    .input1({4'b0000, inflow}), .input2(adder8bit_3_output1), .output1({overflow, output1}));  // open: inflow, overflow
  adder8bit adder8bit_3 (
    .input1(adder8bit_1_output1), .input2(adder8bit_4_output1), .output1(adder8bit_3_output1));  // open: inflow, overflow
  adder8bit adder8bit_4 (
    .input1({2'b00, multiplier2bit_3_output1, 2'b00}), .input2({multiplier2bit_4_output1, 4'b0000}),
    .output1(adder8bit_4_output1));  // open: inflow, overflow
  multiplier2bit multiplier2bit_2 (
    .input1(input1[1:0]), .input2(input2[3:2]), .overflow(multiplier2bit_2_output1[5:4]),
    .output1(multiplier2bit_2_output1[3:2]));  // open: inflow
  multiplier2bit multiplier2bit_3 (
    .input1(input1[3:2]), .input2(input2[1:0]), .overflow(multiplier2bit_3_output1[5:4]),
    .output1(multiplier2bit_3_output1[3:2]));  // open: inflow
  multiplier2bit multiplier2bit_4 (
    .input1(input1[3:2]), .input2(input2[3:2]), .overflow(multiplier2bit_4_output1[7:6]),
    .output1(multiplier2bit_4_output1[5:4]));  // open: inflow
endmodule

module multiplier8bit (
  input  [7:0] inflow,
  input  [7:0] input1,
  input  [7:0] input2,
  output [7:0] overflow,
  output [7:0] output1
);

  wire [3:0] multiplier4bit_1_output1, multiplier4bit_1_overflow;
  wire [11:4] multiplier4bit_2_output1, multiplier4bit_3_output1;
  wire [15:0] adder16bit_1_output1, adder16bit_3_output1, adder16bit_4_output1;
  wire [15:8] multiplier4bit_4_output1;

  adder16bit adder16bit_1 (
    .input1({{8{1'b0}}, multiplier4bit_1_overflow, multiplier4bit_1_output1}),
    .input2({4'b0000, multiplier4bit_2_output1, 4'b0000}), .output1(adder16bit_1_output1));  // open: inflow, overflow
  multiplier4bit multiplier4bit_1 (
    .input1(input1[3:0]), .input2(input2[3:0]), .overflow(multiplier4bit_1_overflow),
    .output1(multiplier4bit_1_output1));  // open: inflow
  adder16bit adder16bit_2 (
    .input1({{8{1'b0}}, inflow}), .input2(adder16bit_3_output1), .output1({overflow, output1}));  // open: inflow, overflow
  adder16bit adder16bit_3 (
    .input1(adder16bit_1_output1), .input2(adder16bit_4_output1), .output1(adder16bit_3_output1));  // open: inflow, overflow
  adder16bit adder16bit_4 (
    .input1({4'b0000, multiplier4bit_3_output1, 4'b0000}), .input2({multiplier4bit_4_output1, {8{1'b0}}}),
    .output1(adder16bit_4_output1));  // open: inflow, overflow
  multiplier4bit multiplier4bit_2 (
    .input1(input1[3:0]), .input2(input2[7:4]), .overflow(multiplier4bit_2_output1[11:8]),
    .output1(multiplier4bit_2_output1[7:4]));  // open: inflow
  multiplier4bit multiplier4bit_3 (
    .input1(input1[7:4]), .input2(input2[3:0]), .overflow(multiplier4bit_3_output1[11:8]),
    .output1(multiplier4bit_3_output1[7:4]));  // open: inflow
  multiplier4bit multiplier4bit_4 (
    .input1(input1[7:4]), .input2(input2[7:4]), .overflow(multiplier4bit_4_output1[15:12]),
    .output1(multiplier4bit_4_output1[11:8]));  // open: inflow
endmodule

module multiplier16bit (
  input  [15:0] inflow,
  input  [15:0] input1,
  input  [15:0] input2,
  output [15:0] overflow,
  output [15:0] output1
);

  wire [7:0] multiplier8bit_1_output1, multiplier8bit_1_overflow;
  wire [23:8] multiplier8bit_2_output1, multiplier8bit_3_output1;
  wire [31:0] adder32bit_1_output1, adder32bit_3_output1, adder32bit_4_output1;
  wire [31:16] multiplier8bit_4_output1;

  adder32bit adder32bit_1 (
    .input1({{16{1'b0}}, multiplier8bit_1_overflow, multiplier8bit_1_output1}),
    .input2({{8{1'b0}}, multiplier8bit_2_output1, {8{1'b0}}}), .output1(adder32bit_1_output1));  // open: inflow, overflow
  multiplier8bit multiplier8bit_1 (
    .input1(input1[7:0]), .input2(input2[7:0]), .overflow(multiplier8bit_1_overflow),
    .output1(multiplier8bit_1_output1));  // open: inflow
  adder32bit adder32bit_2 (
    .input1({{16{1'b0}}, inflow}), .input2(adder32bit_3_output1), .output1({overflow, output1}));  // open: inflow, overflow
  adder32bit adder32bit_3 (
    .input1(adder32bit_1_output1), .input2(adder32bit_4_output1), .output1(adder32bit_3_output1));  // open: inflow, overflow
  adder32bit adder32bit_4 (
    .input1({{8{1'b0}}, multiplier8bit_3_output1, {8{1'b0}}}),
    .input2({multiplier8bit_4_output1, {16{1'b0}}}), .output1(adder32bit_4_output1));  // open: inflow, overflow
  multiplier8bit multiplier8bit_2 (
    .input1(input1[7:0]), .input2(input2[15:8]), .overflow(multiplier8bit_2_output1[23:16]),
    .output1(multiplier8bit_2_output1[15:8]));  // open: inflow
  multiplier8bit multiplier8bit_3 (
    .input1(input1[15:8]), .input2(input2[7:0]), .overflow(multiplier8bit_3_output1[23:16]),
    .output1(multiplier8bit_3_output1[15:8]));  // open: inflow
  multiplier8bit multiplier8bit_4 (
    .input1(input1[15:8]), .input2(input2[15:8]), .overflow(multiplier8bit_4_output1[31:24]),
    .output1(multiplier8bit_4_output1[23:16]));  // open: inflow
endmodule

module multiplier32bit (
  input  [31:0] inflow,
  input  [31:0] input1,
  input  [31:0] input2,
  output [31:0] overflow,
  output [31:0] output1
);

  wire [15:0] multiplier16bit_1_output1, multiplier16bit_1_overflow;
  wire [47:16] multiplier16bit_2_output1, multiplier16bit_3_output1;
  wire [63:0] adder64bit_1_output1, adder64bit_3_output1, adder64bit_4_output1;
  wire [63:32] multiplier16bit_4_output1;

  adder64bit adder64bit_1 (
    .input1({{32{1'b0}}, multiplier16bit_1_overflow, multiplier16bit_1_output1}),
    .input2({{16{1'b0}}, multiplier16bit_2_output1, {16{1'b0}}}), .output1(adder64bit_1_output1));  // open: inflow, overflow
  multiplier16bit multiplier16bit_1 (
    .input1(input1[15:0]), .input2(input2[15:0]), .overflow(multiplier16bit_1_overflow),
    .output1(multiplier16bit_1_output1));  // open: inflow
  adder64bit adder64bit_2 (
    .input1({{32{1'b0}}, inflow}), .input2(adder64bit_3_output1), .output1({overflow, output1}));  // open: inflow, overflow
  adder64bit adder64bit_3 (
    .input1(adder64bit_1_output1), .input2(adder64bit_4_output1), .output1(adder64bit_3_output1));  // open: inflow, overflow
  adder64bit adder64bit_4 (
    .input1({{16{1'b0}}, multiplier16bit_3_output1, {16{1'b0}}}),
    .input2({multiplier16bit_4_output1, {32{1'b0}}}), .output1(adder64bit_4_output1));  // open: inflow, overflow
  multiplier16bit multiplier16bit_2 (
    .input1(input1[15:0]), .input2(input2[31:16]), .overflow(multiplier16bit_2_output1[47:32]),
    .output1(multiplier16bit_2_output1[31:16]));  // open: inflow
  multiplier16bit multiplier16bit_3 (
    .input1(input1[31:16]), .input2(input2[15:0]), .overflow(multiplier16bit_3_output1[47:32]),
    .output1(multiplier16bit_3_output1[31:16]));  // open: inflow
  multiplier16bit multiplier16bit_4 (
    .input1(input1[31:16]), .input2(input2[31:16]), .overflow(multiplier16bit_4_output1[63:48]),
    .output1(multiplier16bit_4_output1[47:32]));  // open: inflow
endmodule
