// Logisim project fpcomp.circ as structural Verilog
module fneg64 (
  input  [63:0] inval1,
  output [63:0] outval1,
  output isnan1
);

  wire fpnegator_1_p2;

  // Probe on inval1
  // FPNegator #(.fpwidth(64)) fpnegator_1: pin names not known; wires that end beside it: inval1, fpnegator_1_p2
  not not_1 (outval1[63], inval1[63]);
  Comparator #(.width(11)) comparator_1 (.a(inval1[62:52]), .b({11{1'b1}}), .eq(isnan1));  // open: gt, lt
  // Probe on fpnegator_1_p2
  // Probe on {outval1[63], inval1[62:0]}

  assign outval1[62:0] = inval1[62:0];

  // Notes on the sheet:
  //   inval1: initial=0x4040152bd3c36113
endmodule

module fadd64 (
  input  [63:0] in_1,
  input  [63:0] in_2,
  input  [63:0] in_3,
  input  [63:0] inval1,
  input  [63:0] inval2,
  output [63:0] outval1,
  output isnan1
);

  wire comparator_1_eq, comparator_2_eq, comparator_3_gt, hone64_1_contains1, subtractor_1_bout;
  wire [5:0] hone64_1_outval1, multiplexer_3_out, subtractor_4_out, subtractor_5_out;
  wire [10:0] bit_extender_5_out, multiplexer_5_out;
  wire [15:0] bit_extender_3_out, bit_extender_4_out, negator_1_out, subtractor_1_out, subtractor_2_out,
       subtractor_3_out;
  wire [15:6] multiplexer_3_out_2;
  wire [63:0] adder_1_out, bit_extender_1_out, bit_extender_2_out, fpadder_1_out, multiplexer_1_out,
       multiplexer_2_out, multiplexer_4_out, multiplexer_6_out, multiplexer_7_out, multiplexer_8_out,
       multiplexer_9_out, multiplexer_10_out, negator_2_out, negator_3_out, negator_4_out, shifter_1_out,
       shifter_2_out, shifter_3_out;
  wire [63:52] multiplexer_11_out;

  // Probe on inval1
  // Probe on inval2
  assign bit_extender_1_out = {{11{1'b0}}, {1'b1, inval1[51:0]}};  // Bit_Extender bit_extender_1
  assign bit_extender_2_out = {{11{1'b0}}, {1'b1, inval2[51:0]}};  // Bit_Extender bit_extender_2
  Comparator #(.width(11)) comparator_1 (.a(inval1[62:52]), .b({11{1'b1}}), .eq(comparator_1_eq));  // open: gt, lt
  Comparator #(.width(11)) comparator_2 (.a(inval2[62:52]), .b({11{1'b1}}), .eq(comparator_2_eq));  // open: gt, lt
  Multiplexer #(.width(64)) multiplexer_1 (
    .in0(bit_extender_1_out), .in1(bit_extender_2_out), .out(multiplexer_1_out), .sel(subtractor_1_bout));
  Multiplexer #(.width(64)) multiplexer_2 (
    .in0(bit_extender_2_out), .in1(bit_extender_1_out), .out(multiplexer_2_out), .sel(subtractor_1_bout));
  Subtractor #(.width(16)) subtractor_1 (
    .a(subtractor_2_out), .b(subtractor_3_out), .out(subtractor_1_out), .bout(subtractor_1_bout));  // open: bin
  Subtractor #(.width(16)) subtractor_2 (
    .a(bit_extender_3_out), .b(16'h3ff), .out(subtractor_2_out));  // open: bin, bout
  assign bit_extender_3_out = {{5{1'b0}}, inval1[62:52]};  // Bit_Extender bit_extender_3
  or or_1 (isnan1, comparator_1_eq, comparator_2_eq);
  FPAdder #(.fpwidth(64)) fpadder_1 (.a(inval1), .b(inval2), .out(fpadder_1_out));
  Shifter #(.shift("lr"), .width(64)) shifter_1 (
    .in(multiplexer_2_out), .\dist (multiplexer_3_out), .out(shifter_1_out));
  Multiplexer #(.width(16)) multiplexer_3 (
    .in0(subtractor_1_out), .in1(negator_1_out), .out({multiplexer_3_out_2, multiplexer_3_out}),
    .sel(subtractor_1_bout));
  Negator #(.width(16)) negator_1 (.in(subtractor_1_out), .out(negator_1_out));
  Subtractor #(.width(16)) subtractor_3 (
    .a(bit_extender_4_out), .b(16'h3ff), .out(subtractor_3_out));  // open: bin, bout
  assign bit_extender_4_out = {{5{1'b0}}, inval2[62:52]};  // Bit_Extender bit_extender_4
  Comparator #(.width(16)) comparator_3 (
    .a({multiplexer_3_out_2, multiplexer_3_out}), .b(16'h3f), .gt(comparator_3_gt));  // open: eq, lt
  Multiplexer #(.width(64)) multiplexer_4 (
    .in0(shifter_1_out), .in1({64{1'b0}}), .out(multiplexer_4_out), .sel(comparator_3_gt));
  Multiplexer #(.width(11)) multiplexer_5 (
    .in0(inval1[62:52]), .in1(inval2[62:52]), .out(multiplexer_5_out), .sel(subtractor_1_bout));
  Multiplexer #(.width(64)) multiplexer_6 (
    .in0(multiplexer_1_out), .in1(multiplexer_4_out), .out(multiplexer_6_out), .sel(subtractor_1_bout));
  Multiplexer #(.width(64)) multiplexer_7 (
    .in0(multiplexer_4_out), .in1(multiplexer_1_out), .out(multiplexer_7_out), .sel(subtractor_1_bout));
  Negator #(.width(64)) negator_2 (.in(multiplexer_7_out), .out(negator_2_out));
  Multiplexer #(.width(64)) multiplexer_8 (
    .in0(multiplexer_6_out), .in1(negator_3_out), .out(multiplexer_8_out), .sel(inval1[63]));
  Negator #(.width(64)) negator_3 (.in(multiplexer_6_out), .out(negator_3_out));
  Multiplexer #(.width(64)) multiplexer_9 (
    .in0(multiplexer_7_out), .in1(negator_2_out), .out(multiplexer_9_out), .sel(inval2[63]));
  Adder #(.width(64)) adder_1 (.a(multiplexer_8_out), .b(multiplexer_9_out), .out(adder_1_out));  // open: cin, cout
  Negator #(.width(64)) negator_4 (.in(adder_1_out), .out(negator_4_out));
  Comparator #(.width(64)) comparator_4 (.a(adder_1_out), .b({64{1'b0}}), .lt(outval1[63]));  // open: gt, eq
  Multiplexer #(.width(64)) multiplexer_10 (
    .in0(adder_1_out), .in1(negator_4_out), .out(multiplexer_10_out), .sel(outval1[63]));
  hone64 hone64_1 (.inval1(multiplexer_10_out), .outval1(hone64_1_outval1), .contains1(hone64_1_contains1));
  Shifter #(.width(64)) shifter_2 (.in(multiplexer_10_out), .\dist (subtractor_4_out), .out(shifter_2_out));
  Subtractor #(.width(6)) subtractor_4 (
    .a({6{1'b1}}), .b(hone64_1_outval1), .out(subtractor_4_out));  // open: bin, bout
  Shifter #(.shift("lr"), .width(64)) shifter_3 (.in(shifter_2_out), .\dist (6'b001011), .out(shifter_3_out));
  Subtractor #(.width(6)) subtractor_5 (
    .a(subtractor_4_out), .b(6'b001011), .out(subtractor_5_out));  // open: bin, bout
  assign bit_extender_5_out = {{5{subtractor_5_out[5]}}, subtractor_5_out};  // Bit_Extender bit_extender_5
  Multiplexer #(.width(64)) multiplexer_11 (
    .in0({64{1'b0}}), .in1(shifter_3_out), .out({multiplexer_11_out, outval1[51:0]}), .sel(hone64_1_contains1));
  Subtractor #(.width(11)) subtractor_6 (
    .a(multiplexer_5_out), .b(bit_extender_5_out), .out(outval1[62:52]));  // open: bin, bout
  // Probe on fpadder_1_out
  // Probe on fpadder_1_out
  // Probe on outval1

  // Notes on the sheet:
  //   in_1: initial=0x4040152bd3c36113
  //   in_2: initial=0x4061d93f7ced9168
  //   in_3: initial=0xc056ef0d844d013b
  //   inval1: initial=0x4061d93f7ced9168
  //   inval2: initial=0xc056ef0d844d013b
endmodule

module fsub64 (
  input  [63:0] inval1,
  input  [63:0] inval2,
  output [63:0] outval1
);
endmodule

module fmul64 (
  input  [63:0] inval1,
  input  [63:0] inval2,
  output [63:0] outval1
);
endmodule

module fdiv64 (
  input  [63:0] inval1,
  input  [63:0] inval2,
  output [63:0] outval1
);
endmodule

module hone64 (
  input  [63:0] inval1,
  output [5:0] outval1,
  output contains1
);

  wire bitfinder_1_found, not_1_out;
  wire [5:0] bitfinder_1_index, priority_encoder_1_out;

  // Probe on priority_encoder_1_out
  Priority_Encoder #(.select(6)) priority_encoder_1 (
    .in0(inval1[0]), .in1(inval1[1]), .in2(inval1[2]), .in3(inval1[3]), .in4(inval1[4]), .in5(inval1[5]),
    .in6(inval1[6]), .in7(inval1[7]), .in8(inval1[8]), .in9(inval1[9]), .in10(inval1[10]), .in11(inval1[11]),
    .in12(inval1[12]), .in13(inval1[13]), .in14(inval1[14]), .in15(inval1[15]), .in16(inval1[16]),
    .in17(inval1[17]), .in18(inval1[18]), .in19(inval1[19]), .in20(inval1[20]), .in21(inval1[21]),
    .in22(inval1[22]), .in23(inval1[23]), .in24(inval1[24]), .in25(inval1[25]), .in26(inval1[26]),
    .in27(inval1[27]), .in28(inval1[28]), .in29(inval1[29]), .in30(inval1[30]), .in31(inval1[31]),
    .in32(inval1[32]), .in33(inval1[33]), .in34(inval1[34]), .in35(inval1[35]), .in36(inval1[36]),
    .in37(inval1[37]), .in38(inval1[38]), .in39(inval1[39]), .in40(inval1[40]), .in41(inval1[41]),
    .in42(inval1[42]), .in43(inval1[43]), .in44(inval1[44]), .in45(inval1[45]), .in46(inval1[46]),
    .in47(inval1[47]), .in48(inval1[48]), .in49(inval1[49]), .in50(inval1[50]), .in51(inval1[51]),
    .in52(inval1[52]), .in53(inval1[53]), .in54(inval1[54]), .in55(inval1[55]), .in56(inval1[56]),
    .in57(inval1[57]), .in58(inval1[58]), .in59(inval1[59]), .in60(inval1[60]), .in61(inval1[61]),
    .in62(inval1[62]), .in63(inval1[63]), .out(priority_encoder_1_out), .gs(contains1));  // open: en_out, en_in
  BitFinder #(.\type ("high1"), .width(64)) bitfinder_1 (
    .in(inval1), .index(bitfinder_1_index), .found(bitfinder_1_found));
  Multiplexer #(.width(6)) multiplexer_1 (
    .in0(priority_encoder_1_out), .in1({6{1'b0}}), .out(outval1), .sel(not_1_out));
  not not_1 (not_1_out, contains1);
  // Probe on bitfinder_1_index
  // Probe on bitfinder_1_found
  // Probe on outval1

  // Notes on the sheet:
  //   inval1: initial=0xb000000003ff
endmodule
